# Fritzing sketch hcsr04 (saved by Fritzing 0.9.2b)
breadboards: 1

parts:
  Part2 = SRF05 Ultrasonic Rangefinder
  Raspberry_Pi1 = Raspberry Pi 2

nets:
  VCC: Part2.VCC, Raspberry_Pi1.5V
  N1: Part2.Trig, Raspberry_Pi1.GPIO14
  N2: Part2.Echo, Raspberry_Pi1.GPIO15
  GND: Part2.GND, Raspberry_Pi1.GND
